// Logisim project lab1_part1.circ as structural Verilog: 1 circuit, main circuit main
module main (
  input  x,
  input  s,
  input  y,
  output f
);

  wire n7404_1_p3, n7408_1_pin3, n7408_1_pin11;

  // _7404 #(.ShowInternalStructure("true")) 7404_1: pin names not known; wires that end beside it: 1'b1, s, n7404_1_p3, 1'b0
  _7408 #(.ShowInternalStructure("true")) u_7408_1 (
    .pin1(s), .pin2(y), .pin3(n7408_1_pin3), .pin13(n7404_1_p3), .pin12(x), .pin11(n7408_1_pin11));  // open: pin4, pin5, pin6, pin10, pin9, pin8
  // _7432 #(.ShowInternalStructure("true")) 7432_1: pin names not known; wires that end beside it: 1'b1, n7408_1_pin3, n7408_1_pin11, f, 1'b0
endmodule
