// Logisim project lab2_part1.circ as structural Verilog: 3 circuits, main circuit main
module main (
  input  SW0,
  input  SW1,
  input  SW2,
  input  SW3,
  input  SW4,
  input  SW5,
  output LEDR0
);

  mux4to1 mux4to1_1 (.u(SW0), .v(SW1), .w(SW2), .x(SW3), .s0(SW4), .s1(SW5), .m(LEDR0));
endmodule

module mux2to1 (
  input  x,
  input  y,
  input  s,
  output m
);

  wire and_1_out, and_2_out, not_1_out;

  not not_1 (not_1_out, s);
  and and_1 (and_1_out, x, not_1_out);
  and and_2 (and_2_out, y, s);
  or or_1 (m, and_1_out, and_2_out);
endmodule

module mux4to1 (
  input  u,
  input  v,
  input  w,
  input  x,
  input  s0,
  input  s1,
  output m
);

  wire mux2to1_1_m, mux2to1_2_m;

  mux2to1 mux2to1_1 (.x(u), .y(v), .s(s0), .m(mux2to1_1_m));
  mux2to1 mux2to1_2 (.x(w), .y(x), .s(s0), .m(mux2to1_2_m));
  mux2to1 mux2to1_3 (.x(mux2to1_1_m), .y(mux2to1_2_m), .s(s1), .m(m));
endmodule
