// Logisim project lab4_part1.circ as structural Verilog
module Dlatch (
  input  D,
  input  Clk,
  output Qa,
  output Qb
);

  wire n7400_1_pin3, n7400_1_pin11, n7404_1_p3;

  // _7404 #(.ShowInternalStructure("true")) 7404_1: pin names not known; wires that end beside it: 1'b1, D, n7404_1_p3, 1'b0
  _7400 #(.ShowInternalStructure("true")) u_7400_1 (
    .pin1(n7404_1_p3), .pin2(Clk), .pin3(n7400_1_pin3), .pin4(n7400_1_pin3), .pin5(Qa), .pin6(Qb), .pin13(D),
    .pin12(Clk), .pin11(n7400_1_pin11), .pin10(n7400_1_pin11), .pin9(Qb), .pin8(Qa));
endmodule

module MasterSlaveFlipFlop (
  input  D,
  input  Clk,
  output Q
);

  wire dlatch_1_qa, not_1_out;

  not not_1 (not_1_out, Clk);
  Dlatch dlatch_1 (.D(D), .Clk(Clk), .Qa(dlatch_1_qa));  // open: Qb
  Dlatch dlatch_2 (.D(dlatch_1_qa), .Clk(not_1_out), .Qa(Q));  // open: Qb
endmodule
