// Logisim project lab4_part2.circ as structural Verilog: 20 circuits, main circuit main
module main (
  input  [3:0] A,
  input  [2:0] op,
  input  WE,
  input  R
);

  wire hex_decoder_1_s0, hex_decoder_1_s1, hex_decoder_1_s2, hex_decoder_1_s3, hex_decoder_1_s4,
       hex_decoder_1_s5, hex_decoder_1_s6, hex_decoder_2_s0, hex_decoder_2_s1, hex_decoder_2_s2,
       hex_decoder_2_s3, hex_decoder_2_s4, hex_decoder_2_s5, hex_decoder_2_s6, hex_decoder_3_s0,
       hex_decoder_3_s1, hex_decoder_3_s2, hex_decoder_3_s3, hex_decoder_3_s4, hex_decoder_3_s5,
       hex_decoder_3_s6;
  wire [7:0] alu_1_aluout, ALUreg_q;

  HEX_DECODER hex_decoder_1 (
    .D(A), .S0(hex_decoder_1_s0), .S1(hex_decoder_1_s1), .S2(hex_decoder_1_s2), .S3(hex_decoder_1_s3),
    .S4(hex_decoder_1_s4), .S5(hex_decoder_1_s5), .S6(hex_decoder_1_s6));
  ALU alu_1 (.A(A), .B(ALUreg_q[3:0]), .Op(op), .ALUout(alu_1_aluout));
  _7_Segment_Display HEXA (
    .g(hex_decoder_1_s6), .f(hex_decoder_1_s5), .a(hex_decoder_1_s0), .b(hex_decoder_1_s1),
    .e(hex_decoder_1_s4), .d(hex_decoder_1_s3), .c(hex_decoder_1_s2));  // open: dp
  Register ALUreg (.D(alu_1_aluout), .en(WE), .clk(R), .Q(ALUreg_q));  // open: clr
  HEX_DECODER hex_decoder_2 (
    .D(ALUreg_q[7:4]), .S0(hex_decoder_2_s0), .S1(hex_decoder_2_s1), .S2(hex_decoder_2_s2),
    .S3(hex_decoder_2_s3), .S4(hex_decoder_2_s4), .S5(hex_decoder_2_s5), .S6(hex_decoder_2_s6));
  HEX_DECODER hex_decoder_3 (
    .D(ALUreg_q[3:0]), .S0(hex_decoder_3_s0), .S1(hex_decoder_3_s1), .S2(hex_decoder_3_s2),
    .S3(hex_decoder_3_s3), .S4(hex_decoder_3_s4), .S5(hex_decoder_3_s5), .S6(hex_decoder_3_s6));
  _7_Segment_Display HEX_ALU1 (
    .g(hex_decoder_2_s6), .f(hex_decoder_2_s5), .a(hex_decoder_2_s0), .b(hex_decoder_2_s1),
    .e(hex_decoder_2_s4), .d(hex_decoder_2_s3), .c(hex_decoder_2_s2));  // open: dp
  _7_Segment_Display HEX_ALU0 (
    .g(hex_decoder_3_s6), .f(hex_decoder_3_s5), .a(hex_decoder_3_s0), .b(hex_decoder_3_s1),
    .e(hex_decoder_3_s4), .d(hex_decoder_3_s3), .c(hex_decoder_3_s2));  // open: dp
endmodule

module full_adder (
  input  Cin,
  input  A,
  input  B,
  output Cout,
  output S
);

  wire and_1_out, and_2_out, and_3_out, and_4_out, and_5_out, and_6_out, and_7_out, not_1_out, not_2_out,
       not_3_out;

  not not_1 (not_1_out, Cin);
  not not_2 (not_2_out, A);
  not not_3 (not_3_out, B);
  and and_1 (and_1_out, A, B);
  and and_2 (and_2_out, Cin, B);
  and and_3 (and_3_out, Cin, A);
  and and_4 (and_4_out, not_1_out, not_2_out, B);
  and and_5 (and_5_out, not_1_out, A, not_3_out);
  and and_6 (and_6_out, Cin, not_2_out, not_3_out);
  and and_7 (and_7_out, Cin, A, B);
  or or_1 (Cout, and_1_out, and_2_out, and_3_out);
  or or_2 (S, and_4_out, and_5_out, and_6_out, and_7_out);
endmodule

module ripple_carry4 (
  input  Cin,
  input  [3:0] B,
  input  [3:0] A,
  output [3:0] S,
  output Cout
);

  wire full_adder_1_cout, full_adder_2_cout, full_adder_3_cout;

  full_adder full_adder_1 (.Cin(Cin), .A(A[0]), .B(B[0]), .Cout(full_adder_1_cout), .S(S[0]));
  full_adder full_adder_2 (.Cin(full_adder_1_cout), .A(A[1]), .B(B[1]), .Cout(full_adder_2_cout), .S(S[1]));
  full_adder full_adder_3 (.Cin(full_adder_2_cout), .A(A[2]), .B(B[2]), .Cout(full_adder_3_cout), .S(S[2]));
  full_adder full_adder_4 (.Cin(full_adder_3_cout), .A(A[3]), .B(B[3]), .Cout(Cout), .S(S[3]));
endmodule

module op0 (
  input  [3:0] A,
  output [7:0] OPout
);

  wire [3:0] ripple_carry4_1_s;
  wire [7:4] bit_extender_1_out;

  ripple_carry4 ripple_carry4_1 (.Cin(1'b0), .B(4'b0001), .A(A), .S(ripple_carry4_1_s), .Cout(OPout[4]));
  assign {bit_extender_1_out, OPout[3:0]} = {{4{ripple_carry4_1_s[3]}}, ripple_carry4_1_s};  // Bit_Extender bit_extender_1

  assign OPout[7:5] = 3'b000;
endmodule

module op1 (
  input  [3:0] A,
  input  [3:0] B,
  output [7:0] OPout
);

  wire [3:0] ripple_carry4_1_s;
  wire [7:4] bit_extender_1_out;

  ripple_carry4 ripple_carry4_1 (.Cin(1'b0), .B(A), .A(B), .S(ripple_carry4_1_s), .Cout(OPout[4]));
  assign {bit_extender_1_out, OPout[3:0]} = {{4{ripple_carry4_1_s[3]}}, ripple_carry4_1_s};  // Bit_Extender bit_extender_1

  assign OPout[7:5] = 3'b000;
endmodule

module op2 (
  input  [3:0] A,
  input  [3:0] B,
  output [7:0] OPout
);

  wire [3:0] adder_1_out;
  wire [7:4] bit_extender_1_out;

  Adder #(.width(4)) adder_1 (.a(A), .b(B), .out(adder_1_out), .cin(1'b0), .cout(OPout[4]));
  assign {bit_extender_1_out, OPout[3:0]} = {{4{adder_1_out[3]}}, adder_1_out};  // Bit_Extender bit_extender_1

  assign OPout[7:5] = 3'b000;
endmodule

module op3 (
  input  [3:0] A,
  input  [3:0] B,
  output [7:0] OPout
);

  or or_1 (OPout[7], A[3], B[3]);
  xor xor_1 (OPout[3], A[3], B[3]);
  or or_2 (OPout[6], A[2], B[2]);
  or or_3 (OPout[5], A[1], B[1]);
  xor xor_2 (OPout[2], A[2], B[2]);
  or or_4 (OPout[4], A[0], B[0]);
  xor xor_3 (OPout[1], B[1], A[1]);
  xor xor_4 (OPout[0], B[0], A[0]);
endmodule

module op4 (
  input  [3:0] A,
  input  [3:0] B,
  output [7:0] OPout
);

  wire comparator_1_gt, or_1_out;
  wire [7:0] bit_extender_1_out;

  or or_1 (or_1_out, A[0], A[1], A[2], A[3], B[0], B[1], B[2], B[3]);
  assign bit_extender_1_out = {{7{or_1_out}}, or_1_out};  // Bit_Extender bit_extender_1
  Comparator comparator_1 (.a(bit_extender_1_out), .b({8{1'b1}}), .gt(comparator_1_gt));  // open: eq, lt
  Multiplexer #(.width(8)) multiplexer_1 (.in0(8'h1), .in1(bit_extender_1_out), .out(OPout), .sel(comparator_1_gt));
endmodule

module op5 (
  input  [3:0] A,
  input  [3:0] B,
  output [7:0] OPout
);

  wire [2:0] bit_extender_2_out;
  wire [7:0] bit_extender_1_out;

  assign bit_extender_1_out = {{4{1'b0}}, B};  // Bit_Extender bit_extender_1
  Bit_Extender #(.in_width(4), .out_width(3), .\type ("zero")) bit_extender_2 (.in(A), .out(bit_extender_2_out));
  Shifter shifter_1 (.in(bit_extender_1_out), .\dist (bit_extender_2_out), .out(OPout));
endmodule

module ALU (
  input  [3:0] A,
  input  [3:0] B,
  input  [2:0] Op,
  output [7:0] ALUout
);

  wire [7:0] op0_1_opout, op1_1_opout, op2_1_opout, op3_1_opout, op4_1_opout, op5_1_opout;

  op0 op0_1 (.A(A), .OPout(op0_1_opout));
  op1 op1_1 (.A(A), .B(B), .OPout(op1_1_opout));
  op2 op2_1 (.A(A), .B(B), .OPout(op2_1_opout));
  op3 op3_1 (.A(A), .B(B), .OPout(op3_1_opout));
  op4 op4_1 (.A(A), .B(B), .OPout(op4_1_opout));
  op5 op5_1 (.A(A), .B(B), .OPout(op5_1_opout));
  op6 op6_1 (.A(A), .B(B));  // open: OPout
  op7 op7_1 (.A(A), .B(B));  // open: OPout
  Multiplexer #(.select(3), .width(8)) multiplexer_1 (
    .in0(op0_1_opout), .in1(op1_1_opout), .in2(op2_1_opout), .in3(op3_1_opout), .in4(op4_1_opout),
    .in5(op5_1_opout), .out(ALUout), .sel(Op));  // open: in6, in7
endmodule

module HEX0 (
  input  D3,
  input  D2,
  input  D1,
  input  D0,
  output S0
);

  wire and_1_out, and_2_out, and_3_out, and_4_out, and_5_out, and_6_out, and_7_out, not_1_out, not_2_out,
       not_3_out, not_4_out, or_1_out, or_2_out, or_3_out;

  not not_1 (not_1_out, D3);
  not not_2 (not_2_out, D2);
  not not_3 (not_3_out, D1);
  not not_4 (not_4_out, D0);
  and and_1 (and_1_out, not_2_out, not_4_out);
  and and_2 (and_2_out, not_1_out, D1);
  and and_3 (and_3_out, not_1_out, D2);
  and and_4 (and_4_out, D3, not_2_out);
  or or_1 (or_1_out, and_1_out, and_2_out);
  and and_5 (and_5_out, and_3_out, D0);
  and and_6 (and_6_out, D2, D1);
  and and_7 (and_7_out, and_4_out, not_3_out);
  or or_2 (or_2_out, or_1_out, and_5_out);
  or or_3 (or_3_out, and_6_out, and_7_out);
  or or_4 (S0, or_2_out, or_3_out);
endmodule

module HEX1 (
  input  D3,
  input  D2,
  input  D1,
  input  D0,
  output S1
);

  wire and_1_out, and_2_out, and_3_out, and_4_out, and_5_out, and_6_out, and_7_out, and_8_out, not_1_out,
       not_2_out, not_3_out, not_4_out, or_1_out, or_2_out, or_4_out;

  not not_1 (not_1_out, D3);
  not not_2 (not_2_out, D2);
  not not_3 (not_3_out, D1);
  not not_4 (not_4_out, D0);
  and and_1 (and_1_out, not_1_out, not_3_out);
  and and_2 (and_2_out, not_1_out, not_2_out);
  and and_3 (and_3_out, and_1_out, not_4_out);
  and and_4 (and_4_out, not_1_out, D1);
  and and_5 (and_5_out, D3, not_3_out);
  or or_1 (or_1_out, and_2_out, and_3_out);
  and and_6 (and_6_out, not_2_out, not_4_out);
  and and_7 (and_7_out, and_4_out, D0);
  and and_8 (and_8_out, and_5_out, D0);
  or or_2 (or_2_out, or_1_out, and_6_out);
  or or_3 (S1, or_2_out, or_4_out);
  or or_4 (or_4_out, and_7_out, and_8_out);
endmodule

module HEX2 (
  input  D3,
  input  D2,
  input  D1,
  input  D0,
  output S2
);

  wire and_1_out, and_2_out, and_3_out, and_4_out, and_5_out, not_1_out, not_2_out, not_3_out, or_1_out,
       or_2_out, or_3_out;

  not not_1 (not_1_out, D3);
  not not_2 (not_2_out, D2);
  not not_3 (not_3_out, D1);
  and and_1 (and_1_out, not_1_out, not_3_out);
  and and_2 (and_2_out, not_1_out, D0);
  or or_1 (or_1_out, and_1_out, and_2_out);
  and and_3 (and_3_out, not_3_out, D0);
  and and_4 (and_4_out, not_1_out, D2);
  and and_5 (and_5_out, D3, not_2_out);
  or or_2 (or_2_out, or_1_out, and_3_out);
  or or_3 (or_3_out, and_4_out, and_5_out);
  or or_4 (S2, or_2_out, or_3_out);
endmodule

module HEX3 (
  input  D3,
  input  D2,
  input  D1,
  input  D0,
  output S3
);

  wire and_1_out, and_2_out, and_3_out, and_4_out, and_5_out, and_6_out, and_7_out, and_8_out, and_9_out,
       and_10_out, and_11_out, not_1_out, not_2_out, not_3_out, not_4_out, or_1_out, or_2_out, or_3_out,
       or_5_out;

  not not_1 (not_1_out, D3);
  not not_2 (not_2_out, D2);
  not not_3 (not_3_out, D1);
  not not_4 (not_4_out, D0);
  and and_1 (and_1_out, not_1_out, not_2_out);
  and and_2 (and_2_out, not_1_out, D1);
  and and_3 (and_3_out, D2, not_3_out);
  and and_4 (and_4_out, and_1_out, not_4_out);
  and and_5 (and_5_out, and_2_out, not_4_out);
  and and_6 (and_6_out, not_2_out, D1);
  and and_7 (and_7_out, and_3_out, D0);
  and and_8 (and_8_out, D3, not_3_out);
  and and_9 (and_9_out, D3, D2);
  or or_1 (or_1_out, and_4_out, and_5_out);
  and and_10 (and_10_out, and_6_out, D0);
  or or_2 (or_2_out, and_7_out, and_8_out);
  and and_11 (and_11_out, and_9_out, not_4_out);
  or or_3 (or_3_out, or_1_out, and_10_out);
  or or_4 (S3, or_3_out, or_5_out);
  or or_5 (or_5_out, or_2_out, and_11_out);
endmodule

module HEX4 (
  input  D3,
  input  D2,
  input  D1,
  input  D0,
  output S4
);

  wire and_1_out, and_2_out, and_3_out, and_4_out, not_1_out, not_2_out, or_1_out, or_2_out;

  not not_1 (not_1_out, D2);
  not not_2 (not_2_out, D0);
  and and_1 (and_1_out, not_1_out, not_2_out);
  and and_2 (and_2_out, D1, not_2_out);
  and and_3 (and_3_out, D3, D1);
  and and_4 (and_4_out, D3, D2);
  or or_1 (or_1_out, and_1_out, and_2_out);
  or or_2 (or_2_out, and_3_out, and_4_out);
  or or_3 (S4, or_1_out, or_2_out);
endmodule

module HEX5 (
  input  D3,
  input  D2,
  input  D1,
  input  D0,
  output S5
);

  wire and_1_out, and_2_out, and_3_out, and_4_out, and_5_out, and_6_out, and_7_out, and_8_out, not_1_out,
       not_2_out, not_3_out, not_4_out, or_1_out, or_2_out, or_4_out;

  not not_1 (not_1_out, D3);
  not not_2 (not_2_out, D2);
  not not_3 (not_3_out, D1);
  not not_4 (not_4_out, D0);
  and and_1 (and_1_out, not_1_out, not_3_out);
  and and_2 (and_2_out, not_1_out, D2);
  and and_3 (and_3_out, and_1_out, not_4_out);
  and and_4 (and_4_out, and_2_out, not_3_out);
  and and_5 (and_5_out, not_1_out, D2);
  or or_1 (or_1_out, and_3_out, and_4_out);
  and and_6 (and_6_out, and_5_out, not_4_out);
  and and_7 (and_7_out, D3, not_2_out);
  and and_8 (and_8_out, D3, D1);
  or or_2 (or_2_out, or_1_out, and_6_out);
  or or_3 (S5, or_2_out, or_4_out);
  or or_4 (or_4_out, and_7_out, and_8_out);
endmodule

module HEX6 (
  input  D3,
  input  D2,
  input  D1,
  input  D0,
  output S6
);

  wire and_1_out, and_2_out, and_3_out, not_1_out, not_2_out, not_3_out, or_1_out, or_2_out;

  not not_1 (not_1_out, D2);
  not not_2 (not_2_out, D1);
  not not_3 (not_3_out, D0);
  and and_1 (and_1_out, not_1_out, D1);
  and and_2 (and_2_out, D2, not_2_out);
  and and_3 (and_3_out, D2, not_3_out);
  or or_1 (or_1_out, and_1_out, and_2_out);
  or or_2 (or_2_out, and_3_out, D3);
  or or_3 (S6, or_1_out, or_2_out);
endmodule

module HEX_DECODER (
  input  [3:0] D,
  output S0,
  output S1,
  output S2,
  output S3,
  output S4,
  output S5,
  output S6
);

  HEX0 hex0_1 (.D3(D[3]), .D2(D[2]), .D1(D[1]), .D0(D[0]), .S0(S0));
  HEX1 hex1_1 (.D3(D[3]), .D2(D[2]), .D1(D[1]), .D0(D[0]), .S1(S1));
  HEX2 hex2_1 (.D3(D[3]), .D2(D[2]), .D1(D[1]), .D0(D[0]), .S2(S2));
  HEX3 hex3_1 (.D3(D[3]), .D2(D[2]), .D1(D[1]), .D0(D[0]), .S3(S3));
  HEX4 hex4_1 (.D3(D[3]), .D2(D[2]), .D1(D[1]), .D0(D[0]), .S4(S4));
  HEX5 hex5_1 (.D3(D[3]), .D2(D[2]), .D1(D[1]), .D0(D[0]), .S5(S5));
  HEX6 hex6_1 (.D3(D[3]), .D2(D[2]), .D1(D[1]), .D0(D[0]), .S6(S6));
endmodule

module op6 (
  input  [3:0] A,
  input  [3:0] B,
  output [7:0] OPout
);

  wire [2:0] bit_extender_2_out;
  wire [7:0] bit_extender_1_out;

  assign bit_extender_1_out = {{4{1'b0}}, B};  // Bit_Extender bit_extender_1
  Bit_Extender #(.in_width(4), .out_width(3), .\type ("zero")) bit_extender_2 (.in(A), .out(bit_extender_2_out));
  Shifter #(.shift("lr")) shifter_1 (.in(bit_extender_1_out), .\dist (bit_extender_2_out), .out(OPout));
endmodule

module op7 (
  input  [3:0] A,
  input  [3:0] B,
  output [7:0] OPout
);

  wire [7:0] bit_extender_1_out, bit_extender_2_out;

  assign bit_extender_1_out = {{4{1'b0}}, B};  // Bit_Extender bit_extender_1
  assign bit_extender_2_out = {{4{1'b0}}, A};  // Bit_Extender bit_extender_2
  Multiplier multiplier_1 (.a(bit_extender_1_out), .b(bit_extender_2_out), .out(OPout));  // open: cin, cout
endmodule
