// Logisim project lab4_part3.circ as structural Verilog
module shifter_bit (
  input  load_val,
  input  inn,
  input  Clk,
  input  shift,
  input  load_n,
  input  reset,
  output outt
);

  wire multiplexer_1_out, multiplexer_2_out;

  Multiplexer multiplexer_1 (.in0(outt), .in1(inn), .out(multiplexer_1_out), .sel(shift));
  Multiplexer multiplexer_2 (.in0(load_val), .in1(multiplexer_1_out), .out(multiplexer_2_out), .sel(load_n));
  D_Flip_Flop d_ff_1 (.D(multiplexer_2_out), .clk(Clk), .Q(outt), .reset(reset));  // open: Qn, preset
endmodule

module shift_register (
  input  [7:0] LoadVal,
  input  ShiftRight,
  input  ASR,
  input  load_n,
  input  clk,
  input  reset,
  output [7:0] Q
);

  wire multiplexer_1_out;

  Multiplexer multiplexer_1 (.in0(1'b0), .in1(LoadVal[7]), .out(multiplexer_1_out), .sel(ASR));
  shifter_bit shifter_bit_1 (
    .load_val(LoadVal[0]), .inn(Q[1]), .Clk(clk), .shift(ShiftRight), .load_n(load_n), .reset(reset),
    .outt(Q[0]));
  shifter_bit shifter_bit_2 (
    .load_val(LoadVal[1]), .inn(Q[2]), .Clk(clk), .shift(ShiftRight), .load_n(load_n), .reset(reset),
    .outt(Q[1]));
  shifter_bit shifter_bit_3 (
    .load_val(LoadVal[2]), .inn(Q[3]), .Clk(clk), .shift(ShiftRight), .load_n(load_n), .reset(reset),
    .outt(Q[2]));
  shifter_bit shifter_bit_4 (
    .load_val(LoadVal[3]), .inn(Q[4]), .Clk(clk), .shift(ShiftRight), .load_n(load_n), .reset(reset),
    .outt(Q[3]));
  shifter_bit shifter_bit_5 (
    .load_val(LoadVal[4]), .inn(Q[5]), .Clk(clk), .shift(ShiftRight), .load_n(load_n), .reset(reset),
    .outt(Q[4]));
  shifter_bit shifter_bit_6 (
    .load_val(LoadVal[5]), .inn(Q[6]), .Clk(clk), .shift(ShiftRight), .load_n(load_n), .reset(reset),
    .outt(Q[5]));
  shifter_bit shifter_bit_7 (
    .load_val(LoadVal[6]), .inn(Q[7]), .Clk(clk), .shift(ShiftRight), .load_n(load_n), .reset(reset),
    .outt(Q[6]));
  shifter_bit shifter_bit_8 (
    .load_val(LoadVal[7]), .inn(multiplexer_1_out), .Clk(clk), .shift(ShiftRight), .load_n(load_n),
    .reset(reset), .outt(Q[7]));
endmodule
