// Logisim project lab5.circ as structural Verilog
module incrementer4 (
  input  CountEnable,
  input  Clock,
  input  Clear,
  output [3:0] Q
);

  wire and_1_out, and_2_out, and_3_out;

  T_Flip_Flop TFF0 (.T(CountEnable), .clk(Clock), .Q(Q[0]), .reset(Clear));  // open: Qn, preset
  and and_1 (and_1_out, CountEnable, Q[0]);
  T_Flip_Flop TFF1 (.T(and_1_out), .clk(Clock), .Q(Q[1]), .reset(Clear));  // open: Qn, preset
  and and_2 (and_2_out, and_1_out, Q[1]);
  T_Flip_Flop TFF2 (.T(and_2_out), .clk(Clock), .Q(Q[2]), .reset(Clear));  // open: Qn, preset
  and and_3 (and_3_out, and_2_out, Q[2]);
  T_Flip_Flop TFF3 (.T(and_3_out), .clk(Clock), .Q(Q[3]), .reset(Clear));  // open: Qn, preset
endmodule

module handout_example (
  input  Reset,
  input  CountEnable,
  output CounterOut
);

  wire CLK_out, not_1_out, or_1_out;
  wire [3:0] counter_1_q;

  Clock CLK (.out(CLK_out));
  not not_1 (not_1_out, CountEnable);
  or or_1 (or_1_out, CounterOut, not_1_out);
  Counter #(.max('hf), .width(4)) counter_1 (
    .clr(Reset), .load(or_1_out), .up(1'b1), .clk(CLK_out), .D(4'b0000), .Q(counter_1_q));  // open: count, carry
  and and_1 (CounterOut, counter_1_q[0], counter_1_q[1], counter_1_q[2], counter_1_q[3]);
endmodule
