// Logisim project lab6_starter file.circ as structural Verilog
module part_1_state_table (
  input  [2:0] curr_state,
  input  w,
  output [2:0] next_state
);

  wire and_1_out, and_2_out, and_3_out, and_4_out, and_5_out, and_6_out, and_7_out, and_8_out, not_1_out,
       not_2_out, not_3_out, not_4_out;

  not not_1 (not_1_out, curr_state[2]);
  not not_2 (not_2_out, curr_state[1]);
  not not_3 (not_3_out, curr_state[0]);
  not not_4 (not_4_out, w);
  and and_1 (and_1_out, not_1_out, not_3_out, w);
  and and_2 (and_2_out, curr_state[2], curr_state[0], w);
  or or_1 (next_state[2], and_1_out, and_2_out, and_3_out);
  and and_3 (and_3_out, curr_state[1], not_3_out, w);
  and and_4 (and_4_out, not_1_out, curr_state[0], not_4_out);
  and and_5 (and_5_out, not_1_out, curr_state[1], not_3_out, w);
  or or_2 (next_state[1], and_4_out, and_5_out, and_6_out);
  and and_6 (and_6_out, curr_state[2], not_2_out, not_3_out);
  and and_7 (and_7_out, not_2_out, not_3_out, w);
  or or_3 (next_state[0], and_7_out, and_8_out);
  and and_8 (and_8_out, not_1_out, curr_state[0], w);
endmodule

module part_1_FSM (
  input  W,
  input  Enable,
  input  Reset,
  output z
);

  wire and_1_out, and_2_out, Clk_out, not_1_out, not_2_out, not_3_out;
  wire [2:0] state_q, state_table_next_state;

  part_1_state_table state_table (.curr_state(state_q), .w(W), .next_state(state_table_next_state));
  Register #(.width(3)) state (.D(state_table_next_state), .en(Enable), .clk(Clk_out), .Q(state_q), .clr(Reset));
  Clock Clk (.out(Clk_out));
  not not_1 (not_1_out, state_q[1]);
  not not_2 (not_2_out, state_q[2]);
  not not_3 (not_3_out, state_q[0]);
  and and_1 (and_1_out, state_q[0], not_1_out, not_2_out);
  and and_2 (and_2_out, state_q[2], state_q[1], not_3_out);
  xor xor_1 (z, and_1_out, and_2_out);

  // Notes on the sheet:
  //   your state table
  //   state register
  //   output logic (to be completed by you)
endmodule

module part_2_datapath (
  input  ld_alu_out,
  input  [7:0] data_in,
  input  clk,
  input  ld_c,
  input  ld_x,
  input  ld_a,
  input  ld_b,
  input  Reset,
  input  [1:0] alu_select_a,
  input  [1:0] alu_select_b,
  input  alu_op,
  input  ld_r,
  output [7:0] R_B_val,
  output [7:0] R_A_val,
  output [7:0] R_X_val,
  output [7:0] R_C_val,
  output [7:0] data_result
);

  wire [7:0] multiplexer_1_out, multiplexer_2_out, multiplexer_3_out, multiplexer_4_out, part_2_alu_1_alu_out;

  Register R_C (.D(data_in), .en(ld_c), .clk(clk), .Q(R_C_val), .clr(Reset));
  Register R_X (.D(data_in), .en(ld_x), .clk(clk), .Q(R_X_val), .clr(Reset));
  Multiplexer #(.select(2), .width(8)) multiplexer_1 (
    .in0(R_A_val), .in1(R_B_val), .in2(R_C_val), .in3(R_X_val), .out(multiplexer_1_out), .sel(alu_select_a));
  Multiplexer #(.width(8)) multiplexer_2 (
    .in0(data_in), .in1(part_2_alu_1_alu_out), .out(multiplexer_2_out), .sel(ld_alu_out));
  Register R_A (.D(multiplexer_2_out), .en(ld_a), .clk(clk), .Q(R_A_val), .clr(Reset));
  Multiplexer #(.select(2), .width(8)) multiplexer_3 (
    .in0(R_A_val), .in1(R_B_val), .in2(R_C_val), .in3(R_X_val), .out(multiplexer_3_out), .sel(alu_select_b));
  part_2_ALU part_2_alu_1 (
    .input_1(multiplexer_1_out), .input_2(multiplexer_3_out), .ALU_op(alu_op), .ALU_out(part_2_alu_1_alu_out));
  Multiplexer #(.width(8)) multiplexer_4 (
    .in0(data_in), .in1(part_2_alu_1_alu_out), .out(multiplexer_4_out), .sel(ld_alu_out));
  Register R_B (.D(multiplexer_4_out), .en(ld_b), .clk(clk), .Q(R_B_val), .clr(Reset));
  Register R_R (.D(part_2_alu_1_alu_out), .en(ld_r), .clk(clk), .Q(data_result), .clr(Reset));
endmodule

module part_2_ALU (
  input  [7:0] input_1,
  input  [7:0] input_2,
  input  ALU_op,
  output [7:0] ALU_out
);

  wire [7:0] adder_1_out, multiplier_1_out;

  Adder adder_1 (.a(input_1), .b(input_2), .out(adder_1_out));  // open: cin, cout
  Multiplier multiplier_1 (.a(input_1), .b(input_2), .out(multiplier_1_out));  // open: cin, cout
  Multiplexer #(.width(8)) multiplexer_1 (.in0(adder_1_out), .in1(multiplier_1_out), .out(ALU_out), .sel(ALU_op));
endmodule

module part_2_state_table (
  input  [3:0] state,
  output ld_a,
  output ld_b,
  output ld_c,
  output ld_x,
  output [1:0] alu_select_a,
  output [1:0] alu_select_b,
  output ld_alu_out,
  output alu_op,
  output ld_r,
  output [3:0] next_state
);

  part_2_ld_a_state_table part_2_ld_a_state_table_1 (.state(state), .ld_a(ld_a));
  part_2_ld_b_state_table part_2_ld_b_state_table_1 (.state(state), .ld_b(ld_b));
  part_2_ld_c_state_table part_2_ld_c_state_table_1 (.state(state), .ld_c(ld_c));
  part_2_ld_x_state_table part_2_ld_x_state_table_1 (.state(state), .ld_x(ld_x));
  part_2_alu_select_a_state_table part_2_alu_select_a_state_table_1 (.state(state), .alu_select_a(alu_select_a));
  part_2_alu_select_b_state_table part_2_alu_select_b_state_table_1 (.state(state), .alu_select_b(alu_select_b));
  part_2_ld_alu_out_state_table part_2_ld_alu_out_state_table_1 (.state(state), .ld_alu_out(ld_alu_out));
  part_2_alu_op_state_table part_2_alu_op_state_table_1 (.state(state), .alu_op(alu_op));
  part_2_ld_r_state_table part_2_ld_r_state_table_1 (.state(state), .ld_r(ld_r));
  part_2_next_state part_2_next_state_1 (.state(state), .next_state(next_state));
endmodule

module part_2_ld_a_state_table (
  input  [3:0] state,
  output ld_a
);

  wire not_1_out, not_2_out;

  not not_1 (not_1_out, state[3]);
  not not_2 (not_2_out, state[0]);
  and and_1 (ld_a, not_1_out, not_2_out);
endmodule

module part_2_ld_b_state_table (
  input  [3:0] state,
  output ld_b
);

  wire and_1_out, and_2_out, not_1_out, not_2_out;

  not not_1 (not_1_out, state[1]);
  not not_2 (not_2_out, state[0]);
  and and_1 (and_1_out, state[3], not_1_out, not_2_out);
  and and_2 (and_2_out, state[2], state[1], not_2_out);
  or or_1 (ld_b, and_1_out, and_2_out);
endmodule

module part_2_ld_c_state_table (
  input  [3:0] state,
  output ld_c
);

  wire not_1_out;

  not not_1 (not_1_out, state[2]);
  and and_1 (ld_c, state[3], not_1_out, state[1], state[0]);
endmodule

module part_2_ld_x_state_table (
  input  [3:0] state,
  output ld_x
);

  wire not_1_out, not_2_out;

  not not_1 (not_1_out, state[2]);
  not not_2 (not_2_out, state[0]);
  and and_1 (ld_x, state[3], not_1_out, state[1], not_2_out);
endmodule

module part_2_alu_select_a_state_table (
  input  [3:0] state,
  output [1:0] alu_select_a
);

  wire and_2_out, and_3_out, and_4_out, not_1_out, not_2_out, not_3_out;

  not not_1 (not_1_out, state[3]);
  not not_2 (not_2_out, state[2]);
  not not_3 (not_3_out, state[1]);
  and and_1 (alu_select_a[1], not_1_out, state[2]);
  and and_2 (and_2_out, not_1_out, state[2]);
  and and_3 (and_3_out, state[3], not_2_out, not_3_out);
  and and_4 (and_4_out, state[2], state[1]);
  or or_1 (alu_select_a[0], and_2_out, and_3_out, and_4_out);
endmodule

module part_2_alu_select_b_state_table (
  input  [3:0] state,
  output [1:0] alu_select_b
);

  wire and_1_out, and_2_out, and_3_out, and_4_out, and_5_out, and_6_out, not_1_out, not_2_out, not_3_out;

  not not_1 (not_1_out, state[3]);
  not not_2 (not_2_out, state[2]);
  not not_3 (not_3_out, state[1]);
  and and_1 (and_1_out, not_1_out, state[1]);
  and and_2 (and_2_out, not_1_out, state[2]);
  and and_3 (and_3_out, state[3], not_2_out, not_3_out);
  and and_4 (and_4_out, not_3_out, state[0]);
  and and_5 (and_5_out, not_1_out, state[2]);
  and and_6 (and_6_out, state[3], not_2_out, not_3_out);
  or or_1 (alu_select_b[1], and_1_out, and_2_out, and_3_out);
  or or_2 (alu_select_b[0], and_4_out, and_5_out, and_6_out);
endmodule

module part_2_ld_alu_out_state_table (
  input  [3:0] state,
  output ld_alu_out
);

  wire and_1_out, and_2_out, and_3_out, and_4_out, not_1_out, not_2_out, not_3_out, not_4_out;

  not not_1 (not_1_out, state[3]);
  not not_2 (not_2_out, state[2]);
  not not_3 (not_3_out, state[1]);
  not not_4 (not_4_out, state[0]);
  and and_1 (and_1_out, not_1_out, state[1], not_4_out);
  and and_2 (and_2_out, not_1_out, state[2], not_4_out);
  and and_3 (and_3_out, state[3], not_2_out, not_3_out, not_4_out);
  and and_4 (and_4_out, state[2], state[1], not_4_out);
  or or_1 (ld_alu_out, and_1_out, and_2_out, and_3_out, and_4_out);
endmodule

module part_2_alu_op_state_table (
  input  [3:0] state,
  output alu_op
);

  wire and_1_out, and_2_out, and_3_out, not_1_out, not_2_out, not_3_out;

  not not_1 (not_1_out, state[3]);
  not not_2 (not_2_out, state[2]);
  not not_3 (not_3_out, state[1]);
  and and_1 (and_1_out, not_1_out, state[1]);
  and and_2 (and_2_out, not_1_out, state[2]);
  and and_3 (and_3_out, state[3], not_2_out, not_3_out);
  or or_1 (alu_op, and_1_out, and_2_out, and_3_out);
endmodule

module part_2_ld_r_state_table (
  input  [3:0] state,
  output ld_r
);

  wire and_1_out, and_2_out, and_3_out, and_4_out, and_5_out, not_1_out, not_2_out, not_3_out;

  not not_1 (not_1_out, state[3]);
  not not_2 (not_2_out, state[2]);
  not not_3 (not_3_out, state[1]);
  and and_1 (and_1_out, not_1_out, state[1]);
  and and_2 (and_2_out, not_1_out, state[2]);
  and and_3 (and_3_out, state[3], not_2_out, not_3_out);
  and and_4 (and_4_out, state[2], state[1]);
  and and_5 (and_5_out, not_1_out, state[0]);
  or or_1 (ld_r, and_1_out, and_2_out, and_3_out, and_4_out, and_5_out);
endmodule

module part_2_next_state (
  input  [3:0] state,
  output [3:0] next_state
);

  wire and_1_out, and_2_out, and_3_out, and_4_out, and_5_out, and_6_out, and_7_out, and_8_out, and_9_out,
       and_10_out, and_11_out, and_12_out, and_13_out, and_14_out, not_1_out, not_2_out, not_3_out, not_4_out;

  not not_1 (not_1_out, state[3]);
  not not_2 (not_2_out, state[2]);
  not not_3 (not_3_out, state[1]);
  not not_4 (not_4_out, state[0]);
  and and_1 (and_1_out, not_2_out, not_3_out, not_4_out);
  and and_2 (and_2_out, state[3], not_2_out);
  and and_3 (and_3_out, state[3], not_3_out);
  and and_4 (and_4_out, state[2], state[1], state[0]);
  and and_5 (and_5_out, not_2_out, not_3_out, not_4_out);
  and and_6 (and_6_out, state[2], state[0]);
  and and_7 (and_7_out, state[2], state[1]);
  and and_8 (and_8_out, state[1], state[0]);
  and and_9 (and_9_out, state[3], not_3_out, not_4_out);
  and and_10 (and_10_out, not_1_out, state[2], not_4_out);
  and and_11 (and_11_out, not_1_out, not_2_out, not_3_out, state[0]);
  and and_12 (and_12_out, state[1], not_4_out);
  and and_13 (and_13_out, state[2], not_4_out);
  and and_14 (and_14_out, state[3], not_4_out);
  or or_1 (next_state[3], and_1_out, and_2_out, and_3_out, and_4_out);
  or or_2 (next_state[2], and_5_out, and_6_out, and_7_out);
  or or_3 (next_state[1], and_8_out, and_9_out, and_10_out);
  or or_4 (next_state[0], and_11_out, and_12_out, and_13_out, and_14_out);
endmodule

module part_2_FSM (
  input  [7:0] data_in,
  input  Enable,
  input  Reset
);

  wire Clk_out, not_1_out, part_2_state_table_1_alu_op, part_2_state_table_1_ld_a,
       part_2_state_table_1_ld_alu_out, part_2_state_table_1_ld_b, part_2_state_table_1_ld_c,
       part_2_state_table_1_ld_r, part_2_state_table_1_ld_x;
  wire [1:0] part_2_state_table_1_alu_select_a, part_2_state_table_1_alu_select_b;
  wire [3:0] part_2_state_table_1_next_state, register_1_q;
  wire [7:0] part_2_datapath_1_data_result, part_2_datapath_1_r_a_val, part_2_datapath_1_r_b_val,
       part_2_datapath_1_r_c_val, part_2_datapath_1_r_x_val;

  part_2_state_table part_2_state_table_1 (
    .state(register_1_q), .ld_a(part_2_state_table_1_ld_a), .ld_b(part_2_state_table_1_ld_b),
    .ld_c(part_2_state_table_1_ld_c), .ld_x(part_2_state_table_1_ld_x),
    .alu_select_a(part_2_state_table_1_alu_select_a), .alu_select_b(part_2_state_table_1_alu_select_b),
    .ld_alu_out(part_2_state_table_1_ld_alu_out), .alu_op(part_2_state_table_1_alu_op),
    .ld_r(part_2_state_table_1_ld_r), .next_state(part_2_state_table_1_next_state));
  Register #(.width(4)) register_1 (
    .D(part_2_state_table_1_next_state), .en(Enable), .clk(Clk_out), .Q(register_1_q), .clr(not_1_out));
  not not_1 (not_1_out, Reset);
  Clock Clk (.out(Clk_out));
  Hex_Digit_Display hex_digit_display_1 (.value(data_in[7:4]));  // open: dp
  Hex_Digit_Display hex_digit_display_2 (.value(data_in[3:0]));  // open: dp
  part_2_datapath part_2_datapath_1 (
    .ld_alu_out(part_2_state_table_1_ld_alu_out), .data_in(data_in), .clk(Clk_out),
    .ld_c(part_2_state_table_1_ld_c), .ld_x(part_2_state_table_1_ld_x), .ld_a(part_2_state_table_1_ld_a),
    .ld_b(part_2_state_table_1_ld_b), .Reset(not_1_out), .alu_select_a(part_2_state_table_1_alu_select_a),
    .alu_select_b(part_2_state_table_1_alu_select_b), .alu_op(part_2_state_table_1_alu_op),
    .ld_r(part_2_state_table_1_ld_r), .R_B_val(part_2_datapath_1_r_b_val),
    .R_A_val(part_2_datapath_1_r_a_val), .R_X_val(part_2_datapath_1_r_x_val),
    .R_C_val(part_2_datapath_1_r_c_val), .data_result(part_2_datapath_1_data_result));
  Hex_Digit_Display hex_digit_display_3 (.value(part_2_datapath_1_r_b_val[7:4]));  // open: dp
  Hex_Digit_Display hex_digit_display_4 (.value(part_2_datapath_1_r_b_val[3:0]));  // open: dp
  Hex_Digit_Display hex_digit_display_5 (.value(part_2_datapath_1_r_c_val[7:4]));  // open: dp
  Hex_Digit_Display hex_digit_display_6 (.value(part_2_datapath_1_data_result[7:4]));  // open: dp
  Hex_Digit_Display hex_digit_display_7 (.value(part_2_datapath_1_r_a_val[7:4]));  // open: dp
  Hex_Digit_Display hex_digit_display_8 (.value(part_2_datapath_1_r_x_val[7:4]));  // open: dp
  Hex_Digit_Display hex_digit_display_9 (.value(part_2_datapath_1_r_x_val[3:0]));  // open: dp
  Hex_Digit_Display hex_digit_display_10 (.value(part_2_datapath_1_r_c_val[3:0]));  // open: dp
  Hex_Digit_Display hex_digit_display_11 (.value(part_2_datapath_1_data_result[3:0]));  // open: dp
  LED led_1 (.in(part_2_datapath_1_data_result[0]));
  LED led_2 (.in(part_2_datapath_1_data_result[1]));
  LED led_3 (.in(part_2_datapath_1_data_result[2]));
  LED led_4 (.in(part_2_datapath_1_data_result[3]));
  LED led_5 (.in(part_2_datapath_1_data_result[4]));
  LED led_6 (.in(part_2_datapath_1_data_result[5]));
  LED led_7 (.in(part_2_datapath_1_data_result[6]));
  LED led_8 (.in(part_2_datapath_1_data_result[7]));
  Hex_Digit_Display hex_digit_display_12 (.value(part_2_datapath_1_r_a_val[3:0]));  // open: dp
endmodule

module F2 (
  input  F_2,
  input  F_1,
  input  F_0,
  input  W,
  output B2
);

  wire and_1_out, and_2_out, and_3_out, and_4_out, not_1_out, not_2_out, not_3_out, not_4_out, not_5_out,
       not_6_out;

  and and_1 (and_1_out, F_2, F_0);
  and and_2 (and_2_out, F_2, F_1);
  not not_1 (not_1_out, F_2);
  not not_2 (not_2_out, F_0);
  not not_3 (not_3_out, F_1);
  not not_4 (not_4_out, F_2);
  not not_5 (not_5_out, F_0);
  not not_6 (not_6_out, W);
  and and_3 (and_3_out, not_1_out, not_2_out, not_3_out);
  and and_4 (and_4_out, not_4_out, not_5_out, not_6_out);
  or or_1 (B2, and_1_out, and_2_out, and_3_out, and_4_out);
endmodule

module F1 (
  input  F_2,
  input  F_1,
  input  F_0,
  input  W,
  output B1
);

  wire and_1_out, not_1_out;

  not not_1 (not_1_out, F_1);
  and and_1 (and_1_out, F_2, not_1_out, F_0);
  or or_1 (B1, and_1_out, W);
endmodule

module F0 (
  input  F_2,
  input  F_1,
  input  F_0,
  input  W,
  output B2
);

  wire and_1_out, and_2_out, not_1_out, not_2_out;

  LED led_1 (.in(F_1));
  not not_1 (not_1_out, F_2);
  and and_1 (and_1_out, not_1_out, W, F_0);
  not not_2 (not_2_out, F_0);
  and and_2 (and_2_out, F_2, not_2_out, W);
  or or_1 (B2, and_1_out, and_2_out);
endmodule
